# Fritzing sketch FritzingSketch (saved by Fritzing 1.0.5)
breadboards: 2

parts:
  LCD1 = LCD screen  # not connected
  Nano = Arduino Nano (Rev3.0)
  S1 = Pushbutton [package="[SMD]"]
  S2 = Pushbutton [package="[SMD]"]
  S4 = Pushbutton [package="[SMD]"]
  SP1 = SPEAKER [package=pcb_mount_speaker]
  DFRobot_DFPlayer_Mini1 = DFRobot DFPlayer Mini [part_number=DFR0299]
  S3 = Pushbutton [package="[SMD]"]

nets (from the schematic view):
  N1: Nano.GND, S1.Pin_3, S1.Pin_4, S2.Pin_3, S2.Pin_4, S4.Pin_3, S4.Pin_4, DFRobot_DFPlayer_Mini1.GND-1, DFRobot_DFPlayer_Mini1.GND-2, S3.Pin_3, S3.Pin_4
  N2: Nano.D2, S1.Pin_1, S1.Pin_2
  N3: Nano.D3, S2.Pin_1, S2.Pin_2
  N4: Nano.D4, S3.Pin_1, S3.Pin_2
  N5: Nano.D6, S4.Pin_1, S4.Pin_2
  N6: Nano.D7, DFRobot_DFPlayer_Mini1.BUSY
  N7: Nano.D10, DFRobot_DFPlayer_Mini1.TX
  N8: Nano.D11/MOSI, DFRobot_DFPlayer_Mini1.RX
  5V: Nano.5V, DFRobot_DFPlayer_Mini1.VCC
  N9: SP1.+, DFRobot_DFPlayer_Mini1.SPK_2
  N10: SP1.-, DFRobot_DFPlayer_Mini1.SPK_1

// code stored in the sketch: DanilOS.ino
#include <Wire.h>
#include <LiquidCrystal_I2C.h>
#include "screen_logo.h"
#include "screen_mp3.h"
#include "screen_menu.h"

LiquidCrystal_I2C lcd(0x27, 16, 2);
DanilScreen currentScreen = SCREEN_BOOT;

void setup() {
  lcd.begin();
  lcd.backlight();

  pinMode(2, INPUT_PULLUP); // prev
  pinMode(3, INPUT_PULLUP); // next
  pinMode(4, INPUT_PULLUP); // play/pause / enter
  pinMode(5, INPUT_PULLUP); // back
  pinMode(6, INPUT_PULLUP); // fn

  showSquirrelLogo(lcd);
  currentScreen = SCREEN_MENU;
}

void loop() {
  if (!digitalRead(5)) {
    currentScreen = SCREEN_MENU;
    delay(250);
  }

  switch (currentScreen) {
    case SCREEN_MENU:
      updateMenu(lcd, currentScreen);
      break;
    case SCREEN_MP3:
      updateScreenMP3(lcd);
      break;
  }
}
